// Logisim project mockup.circ as structural Verilog: 12 circuits, main circuit alu
module main (
);

  wire and_1_out, compare_1_res, exmem_1_mem_mode, idex_1_alu_in1_sel, idex_1_alu_in2_sel, idex_1_alu_mod,
       idex_1_is_cond, instr_decoder_1_alu_in1_sel, instr_decoder_1_alu_in2_sel, instr_decoder_1_alu_mod,
       instr_decoder_1_is_cond, instr_decoder_1_mem_mode, instr_decoder_1_nextpc_sel, not_1_out;
  wire [1:0] exmem_1_rf_in_sel, idex_1_nextpc_sel, idex_1_rf_in_sel, instr_decoder_1_rf_in_sel,
       memwb_1_rf_in_sel;
  wire [2:0] exmem_1_funct3, idex_1_alu_op, idex_1_funct3, instr_decoder_1_alu_op, instr_decoder_1_funct3;
  wire [4:0] exmem_1_rwrite, idex_1_rwrite, instr_decoder_1_rread1, instr_decoder_1_rread2,
       instr_decoder_1_rwrite, memwb_1_rwrite;
  wire [8:0] multiplexer_4_out;
  wire [31:0] adder_1_out, adder_2_out, alu_1_alu_out, data_mem_1_mem_out, exmem_1_alu_out, exmem_1_pcplus4,
       exmem_1_reg2, idex_1_imm, idex_1_pc, idex_1_reg1, idex_1_reg2, ifid_1_instr, ifid_1_pc,
       instr_decoder_1_imm, instr_mem_1_instr, memwb_1_alu_out, memwb_1_mem_out, memwb_1_pcplus4,
       multiplexer_1_out, multiplexer_2_out, multiplexer_3_out, multiplexer_5_out, pc_1_curpc,
       regfile_1_reg1_out, regfile_1_reg2_out;

  Adder #(.width(32)) adder_1 (.a(pc_1_curpc), .b(32'h4), .out(adder_1_out));  // open: cin, cout
  Multiplexer #(.width(32)) multiplexer_1 (
    .in0(adder_1_out), .in1(alu_1_alu_out), .out(multiplexer_1_out), .sel(multiplexer_4_out[0]));
  pc pc_1 (.nextpc(multiplexer_1_out), .curpc(pc_1_curpc));
  instr_mem instr_mem_1 (.addr(pc_1_curpc), .instr(instr_mem_1_instr));
  ifid ifid_1 (.instr_in(instr_mem_1_instr), .pc_in(pc_1_curpc), .instr(ifid_1_instr), .pc(ifid_1_pc));
  instr_decoder instr_decoder_1 (
    .instr(ifid_1_instr), .rread1(instr_decoder_1_rread1), .rread2(instr_decoder_1_rread2),
    .imm(instr_decoder_1_imm), .alu_in1_sel(instr_decoder_1_alu_in1_sel),
    .alu_in2_sel(instr_decoder_1_alu_in2_sel), .alu_op(instr_decoder_1_alu_op),
    .alu_mod(instr_decoder_1_alu_mod), .funct3(instr_decoder_1_funct3), .is_cond(instr_decoder_1_is_cond),
    .nextpc_sel(instr_decoder_1_nextpc_sel), .mem_mode(instr_decoder_1_mem_mode),
    .rf_in_sel(instr_decoder_1_rf_in_sel), .rwrite(instr_decoder_1_rwrite));
  regfile regfile_1 (
    .reg1_sel(instr_decoder_1_rread1), .reg2_sel(instr_decoder_1_rread2), .write_data(multiplexer_5_out),
    .write_sel(memwb_1_rwrite), .reg1_out(regfile_1_reg1_out), .reg2_out(regfile_1_reg2_out));
  idex idex_1 (
    .rwrite_in(instr_decoder_1_rwrite), .imm_in(instr_decoder_1_imm),
    .alu_in1_sel_in(instr_decoder_1_alu_in1_sel), .alu_in2_sel_in(instr_decoder_1_alu_in2_sel),
    .pc_in(ifid_1_pc), .alu_op_in(instr_decoder_1_alu_op), .alu_mod_in(instr_decoder_1_alu_mod),
    .funct3_in(instr_decoder_1_funct3), .is_cond_in(instr_decoder_1_is_cond),
    .nextpc_sel_in(instr_decoder_1_nextpc_sel), .reg1_in(regfile_1_reg1_out), .reg2_in(regfile_1_reg2_out),
    .mem_mode_in(instr_decoder_1_mem_mode), .rf_in_sel_in(instr_decoder_1_rf_in_sel), .imm(idex_1_imm),
    .alu_in1_sel(idex_1_alu_in1_sel), .alu_in2_sel(idex_1_alu_in2_sel), .pc(idex_1_pc),
    .alu_op(idex_1_alu_op), .alu_mod(idex_1_alu_mod), .funct3(idex_1_funct3), .is_cond(idex_1_is_cond),
    .nextpc_sel(idex_1_nextpc_sel[0]), .mem_mode(idex_1_nextpc_sel[1]), .rf_in_sel(idex_1_rf_in_sel),
    .rwrite(idex_1_rwrite), .reg1(idex_1_reg1), .reg2(idex_1_reg2));
  Multiplexer #(.width(32)) multiplexer_2 (
    .in0(idex_1_reg1), .in1(idex_1_pc), .out(multiplexer_2_out), .sel(idex_1_alu_in1_sel));
  Multiplexer #(.width(32)) multiplexer_3 (
    .in0(idex_1_reg2), .in1(idex_1_imm), .out(multiplexer_3_out), .sel(idex_1_alu_in2_sel));
  Adder #(.width(32)) adder_2 (.a(32'h4), .b(idex_1_pc), .out(adder_2_out));  // open: cin, cout
  alu alu_1 (
    .alu_in1(multiplexer_2_out), .alu_in2(multiplexer_3_out), .alu_op(idex_1_alu_op),
    .alu_mod(idex_1_alu_mod), .alu_out(alu_1_alu_out));
  not not_1 (not_1_out, compare_1_res);
  compare compare_1 (.in1(idex_1_reg1), .in2(idex_1_reg2), .funct3(idex_1_funct3), .res(compare_1_res));
  exmem exmem_1 (
    .alu_out_in(alu_1_alu_out), .reg2_in(idex_1_reg2), .funct3_in(idex_1_funct3),
    .mem_mode_in(multiplexer_4_out[1]), .rf_in_sel_in(multiplexer_4_out[3:2]),
    .rwrite_in(multiplexer_4_out[8:4]), .pcplus4_in(adder_2_out), .alu_out(exmem_1_alu_out),
    .reg2(exmem_1_reg2), .funct3(exmem_1_funct3), .mem_mode(exmem_1_mem_mode), .rf_in_sel(exmem_1_rf_in_sel),
    .rwrite(exmem_1_rwrite), .pcplus4(exmem_1_pcplus4));
  and and_1 (and_1_out, not_1_out, idex_1_is_cond);
  Multiplexer #(.width(9)) multiplexer_4 (
    .in0({idex_1_rwrite, idex_1_rf_in_sel, idex_1_nextpc_sel}), .in1({9{1'b0}}), .out(multiplexer_4_out),
    .sel(and_1_out));
  data_mem data_mem_1 (
    .addr(exmem_1_alu_out), .write_data(exmem_1_reg2), .funct3(exmem_1_funct3), .mem_mode(exmem_1_mem_mode),
    .mem_out(data_mem_1_mem_out));
  memwb memwb_1 (
    .pcplus4_in(exmem_1_pcplus4), .alu_out_in(exmem_1_alu_out), .mem_out_in(data_mem_1_mem_out),
    .rf_in_sel_in(exmem_1_rf_in_sel), .rwrite_in(exmem_1_rwrite), .pcplus4(memwb_1_pcplus4),
    .alu_out(memwb_1_alu_out), .mem_out(memwb_1_mem_out), .rf_in_sel(memwb_1_rf_in_sel),
    .rwrite(memwb_1_rwrite));
  Multiplexer #(.select(2), .width(32)) multiplexer_5 (
    .in0(memwb_1_alu_out), .in1(memwb_1_mem_out), .in2(memwb_1_pcplus4), .out(multiplexer_5_out),
    .sel(memwb_1_rf_in_sel));  // open: in3

  // Notes on the sheet:
  //   Fetch
  //   Decode
  //   Instead of this extra adder, just propagate both PC and PC+4
  //   Execute
  //   Memory
  //   Writeback
endmodule

module alu (
  input  [31:0] alu_in1,
  input  [31:0] alu_in2,
  input  [2:0] alu_op,
  input  alu_mod,
  output [31:0] alu_out
);
endmodule

module data_mem (
  input  [31:0] addr,
  input  [31:0] write_data,
  input  [2:0] funct3,
  input  mem_mode,
  output [31:0] mem_out
);
endmodule

module instr_decoder (
  input  [31:0] instr,
  output [4:0] rread1,
  output [4:0] rread2,
  output [31:0] imm,
  output alu_in1_sel,
  output alu_in2_sel,
  output [2:0] alu_op,
  output alu_mod,
  output [2:0] funct3,
  output is_cond,
  output nextpc_sel,
  output mem_mode,
  output [1:0] rf_in_sel,
  output [4:0] rwrite
);
endmodule

module instr_mem (
  input  [31:0] addr,
  output [31:0] instr
);
endmodule

module pc (
  input  [31:0] nextpc,
  output [31:0] curpc
);
endmodule

module regfile (
  input  [4:0] reg1_sel,
  input  [4:0] reg2_sel,
  input  [31:0] write_data,
  input  [4:0] write_sel,
  output [31:0] reg1_out,
  output [31:0] reg2_out
);
endmodule

module ifid (
  input  [31:0] pc_in,
  input  [31:0] instr_in,
  output [31:0] pc,
  output [31:0] instr
);
endmodule

module idex (
  input  [31:0] pc_in,
  input  [31:0] reg1_in,
  input  [31:0] reg2_in,
  input  [31:0] imm_in,
  input  alu_in1_sel_in,
  input  alu_in2_sel_in,
  input  [2:0] alu_op_in,
  input  alu_mod_in,
  input  [2:0] funct3_in,
  input  is_cond_in,
  input  nextpc_sel_in,
  input  mem_mode_in,
  input  [1:0] rf_in_sel_in,
  input  [4:0] rwrite_in,
  output [31:0] pc,
  output [31:0] reg1,
  output [31:0] reg2,
  output [31:0] imm,
  output alu_in1_sel,
  output alu_in2_sel,
  output [2:0] alu_op,
  output alu_mod,
  output [2:0] funct3,
  output is_cond,
  output nextpc_sel,
  output mem_mode,
  output [1:0] rf_in_sel,
  output [4:0] rwrite
);
endmodule

module compare (
  input  [31:0] in1,
  input  [31:0] in2,
  input  [2:0] funct3,
  output res
);
endmodule

module exmem (
  input  [31:0] pcplus4_in,
  input  [31:0] alu_out_in,
  input  [31:0] reg2_in,
  input  [2:0] funct3_in,
  input  mem_mode_in,
  input  [1:0] rf_in_sel_in,
  input  [4:0] rwrite_in,
  output [31:0] pcplus4,
  output [31:0] alu_out,
  output [31:0] reg2,
  output [2:0] funct3,
  output mem_mode,
  output [1:0] rf_in_sel,
  output [4:0] rwrite
);
endmodule

module memwb (
  input  [31:0] pcplus4_in,
  input  [31:0] alu_out_in,
  input  [31:0] mem_out_in,
  input  [1:0] rf_in_sel_in,
  input  [4:0] rwrite_in,
  output [31:0] pcplus4,
  output [31:0] alu_out,
  output [31:0] mem_out,
  output [1:0] rf_in_sel,
  output [4:0] rwrite
);
endmodule
