// Logisim project v1.circ as structural Verilog: 14 circuits, main circuit alu
module main (
);

  wire and_1_out, and_2_out, compare_1_result, exmem_1_mem_mode, hazard_1_id_ex_flush, hazard_1_if_id_flush,
       hazard_1_if_id_we, hazard_1_pc_we, idex_1_alu_in1_sel, idex_1_alu_in2_sel, idex_1_is_cond,
       idex_1_mem_mode, idex_1_nextpc_is_branch, instr_decoder_1_alu_in1_sel, instr_decoder_1_alu_in2_sel,
       instr_decoder_1_is_cond, instr_decoder_1_mem_mode, instr_decoder_1_nextpc_is_branch, not_1_out,
       or_1_out;
  wire [1:0] exmem_1_rf_in_sel, forwarding_1_forward_rs1, forwarding_1_forward_rs2, idex_1_rf_in_sel,
       instr_decoder_1_rf_in_sel, memwb_1_rf_in_sel;
  wire [2:0] exmem_1_funct3, idex_1_alu_op, idex_1_funct3, instr_decoder_1_alu_op, instr_decoder_1_funct3;
  wire [4:0] exmem_1_rd, idex_1_rd, idex_1_rs1, idex_1_rs2, instr_decoder_1_rd, instr_decoder_1_rs1,
       instr_decoder_1_rs2, memwb_1_rd;
  wire [31:0] adder_1_out, alu_1_alu_out, data_mem_1_mem_out, exmem_1_alu_out, exmem_1_pcplus4,
       exmem_1_rs2_val, idex_1_imm, idex_1_pc, idex_1_pcplus4, idex_1_rs1_val, idex_1_rs2_val, ifid_1_instr,
       ifid_1_pc, ifid_1_pcplus4, instr_decoder_1_imm, instr_mem_1_instr, memwb_1_alu_out, memwb_1_mem_out,
       memwb_1_pcplus4, multiplexer_1_out, multiplexer_2_out, multiplexer_3_out, multiplexer_4_out,
       multiplexer_5_out, multiplexer_6_out, pc_1_currentpc, regfile_1_rs1_val, regfile_1_rs2_val;

  Multiplexer #(.width(32)) multiplexer_1 (
    .in0(adder_1_out), .in1(alu_1_alu_out), .out(multiplexer_1_out), .sel(and_2_out));
  pc pc_1 (.nextpc(multiplexer_1_out), .we(hazard_1_pc_we), .currentpc(pc_1_currentpc));
  instr_mem instr_mem_1 (.addr(pc_1_currentpc), .instr(instr_mem_1_instr));
  Adder #(.width(32)) adder_1 (.a(32'h4), .b(pc_1_currentpc), .out(adder_1_out));  // open: cin, cout
  ifid ifid_1 (
    .pcplus4_in(adder_1_out), .instr_in(instr_mem_1_instr), .pc_in(pc_1_currentpc),
    .flush(hazard_1_if_id_flush), .we(hazard_1_if_id_we), .instr(ifid_1_instr), .pcplus4(ifid_1_pcplus4),
    .pc(ifid_1_pc));
  instr_decoder instr_decoder_1 (
    .instr(ifid_1_instr), .alu_in1_sel(instr_decoder_1_alu_in1_sel), .imm(instr_decoder_1_imm),
    .alu_in2_sel(instr_decoder_1_alu_in2_sel), .alu_op(instr_decoder_1_alu_op), .rs1(instr_decoder_1_rs1),
    .rs2(instr_decoder_1_rs2), .is_cond(instr_decoder_1_is_cond),
    .nextpc_is_branch(instr_decoder_1_nextpc_is_branch), .funct3(instr_decoder_1_funct3),
    .mem_mode(instr_decoder_1_mem_mode), .rf_in_sel(instr_decoder_1_rf_in_sel), .rd(instr_decoder_1_rd));
  idex idex_1 (
    .rs1_in(instr_decoder_1_rs1), .rs2_in(instr_decoder_1_rs2), .is_cond_in(instr_decoder_1_is_cond),
    .nextpc_is_branch_in(instr_decoder_1_nextpc_is_branch), .alu_op_in(instr_decoder_1_alu_op),
    .rd_in(instr_decoder_1_rd), .pc_in(ifid_1_pc), .imm_in(instr_decoder_1_imm),
    .alu_in2_sel_in(instr_decoder_1_alu_in2_sel), .funct3_in(instr_decoder_1_funct3),
    .pcplus4_in(ifid_1_pcplus4), .rf_in_sel_in(instr_decoder_1_rf_in_sel),
    .alu_in1_sel_in(instr_decoder_1_alu_in1_sel), .mem_mode_in(instr_decoder_1_mem_mode),
    .flush(hazard_1_id_ex_flush), .rs1_val_in(regfile_1_rs1_val), .rs2_val_in(regfile_1_rs2_val),
    .is_cond(idex_1_is_cond), .nextpc_is_branch(idex_1_nextpc_is_branch), .alu_op(idex_1_alu_op),
    .rf_in_sel(idex_1_rf_in_sel), .pc(idex_1_pc), .imm(idex_1_imm), .alu_in2_sel(idex_1_alu_in2_sel),
    .funct3(idex_1_funct3), .mem_mode(idex_1_mem_mode), .pcplus4(idex_1_pcplus4),
    .alu_in1_sel(idex_1_alu_in1_sel), .rs1(idex_1_rs1), .rs2(idex_1_rs2), .rd(idex_1_rd),
    .rs1_val(idex_1_rs1_val), .rs2_val(idex_1_rs2_val));
  regfile regfile_1 (
    .rs1(instr_decoder_1_rs1), .rs2(instr_decoder_1_rs2), .write_data(multiplexer_6_out), .rd(memwb_1_rd),
    .rs1_val(regfile_1_rs1_val), .rs2_val(regfile_1_rs2_val));
  Multiplexer #(.select(2), .width(32)) multiplexer_2 (
    .in0(idex_1_rs1_val), .in1(exmem_1_alu_out), .in2(memwb_1_alu_out), .in3(memwb_1_mem_out),
    .out(multiplexer_2_out));  // open: sel
  Multiplexer #(.select(2), .width(32)) multiplexer_3 (
    .in0(idex_1_rs2_val), .in1(exmem_1_alu_out), .in2(memwb_1_alu_out), .in3(memwb_1_mem_out),
    .out(multiplexer_3_out));  // open: sel
  hazard hazard_1 (
    .nextpc_is_branch_ex(and_2_out), .rd_ex(idex_1_rd), .rf_in_sel_ex(idex_1_rf_in_sel),
    .rs2_id(instr_decoder_1_rs2), .rs1_id(instr_decoder_1_rs1), .id_ex_flush(hazard_1_id_ex_flush),
    .pc_we(hazard_1_pc_we), .if_id_flush(hazard_1_if_id_flush), .if_id_we(hazard_1_if_id_we));
  Multiplexer #(.width(32)) multiplexer_4 (
    .in0(multiplexer_2_out), .in1(idex_1_pc), .out(multiplexer_4_out), .sel(idex_1_alu_in1_sel));
  Multiplexer #(.width(32)) multiplexer_5 (
    .in0(multiplexer_3_out), .in1(idex_1_imm), .out(multiplexer_5_out), .sel(idex_1_alu_in2_sel));
  compare compare_1 (.a(multiplexer_2_out), .b(multiplexer_3_out), .funct3(idex_1_funct3), .result(compare_1_result));
  alu alu_1 (.a(multiplexer_4_out), .b(multiplexer_5_out), .alu_op(idex_1_alu_op), .alu_out(alu_1_alu_out));
  and and_1 (and_1_out, compare_1_result, idex_1_is_cond);
  not not_1 (not_1_out, idex_1_is_cond);
  or or_1 (or_1_out, not_1_out, and_1_out);
  and and_2 (and_2_out, idex_1_nextpc_is_branch, or_1_out);
  forwarding forwarding_1 (
    .rf_in_sel_wb(memwb_1_rf_in_sel), .rd_wb(memwb_1_rd), .rd_mem(exmem_1_rd),
    .rf_in_sel_mem(exmem_1_rf_in_sel), .rs1_ex(idex_1_rs1), .rs2_ex(idex_1_rs2),
    .forward_rs2(forwarding_1_forward_rs2), .forward_rs1(forwarding_1_forward_rs1));
  exmem exmem_1 (
    .rf_in_sel_in(idex_1_rf_in_sel), .rd_in(idex_1_rd), .alu_out_in(alu_1_alu_out),
    .rs2_val_in(multiplexer_3_out), .funct3_in(idex_1_funct3), .mem_mode_in(idex_1_mem_mode),
    .pcplus4_in(idex_1_pcplus4), .rf_in_sel(exmem_1_rf_in_sel), .rd(exmem_1_rd), .alu_out(exmem_1_alu_out),
    .rs2_val(exmem_1_rs2_val), .funct3(exmem_1_funct3), .mem_mode(exmem_1_mem_mode), .pcplus4(exmem_1_pcplus4));
  memwb memwb_1 (
    .alu_out_in(exmem_1_alu_out), .mem_out_in(data_mem_1_mem_out), .pcplus4_in(exmem_1_pcplus4),
    .rf_in_sel_in(exmem_1_rf_in_sel), .rd_in(exmem_1_rd), .alu_out(memwb_1_alu_out),
    .mem_out(memwb_1_mem_out), .pcplus4(memwb_1_pcplus4), .rf_in_sel(memwb_1_rf_in_sel), .rd(memwb_1_rd));
  data_mem data_mem_1 (
    .addr(exmem_1_alu_out), .write_data(exmem_1_rs2_val), .funct3(exmem_1_funct3),
    .mem_mode(exmem_1_mem_mode), .mem_out(data_mem_1_mem_out));
  Multiplexer #(.select(2), .width(32)) multiplexer_6 (
    .in0(memwb_1_alu_out), .in1(memwb_1_mem_out), .in2(memwb_1_pcplus4), .out(multiplexer_6_out),
    .sel(memwb_1_rf_in_sel));  // open: in3
endmodule

module alu (
  input  [31:0] a,
  input  [31:0] b,
  input  [2:0] alu_op,
  output [31:0] alu_out
);
endmodule

module data_mem (
  input  [31:0] addr,
  input  [31:0] write_data,
  input  [2:0] funct3,
  input  mem_mode,
  output [31:0] mem_out
);
endmodule

module instr_decoder (
  input  [31:0] instr,
  output alu_in1_sel,
  output [31:0] imm,
  output alu_in2_sel,
  output [2:0] alu_op,
  output [4:0] rs1,
  output [4:0] rs2,
  output is_cond,
  output nextpc_is_branch,
  output [2:0] funct3,
  output mem_mode,
  output [1:0] rf_in_sel,
  output [4:0] rd
);
endmodule

module instr_mem (
  input  [31:0] addr,
  output [31:0] instr
);
endmodule

module pc (
  input  [31:0] nextpc,
  input  we,
  output [31:0] currentpc
);
endmodule

module regfile (
  input  [4:0] rs1,
  input  [4:0] rs2,
  input  [31:0] write_data,
  input  [4:0] rd,
  output [31:0] rs1_val,
  output [31:0] rs2_val
);
endmodule

module ifid (
  input  [31:0] pc_in,
  input  [31:0] instr_in,
  input  [31:0] pcplus4_in,
  input  flush,
  input  we,
  output [31:0] pc,
  output [31:0] instr,
  output [31:0] pcplus4
);
endmodule

module idex (
  input  [31:0] pc_in,
  input  alu_in1_sel_in,
  input  [31:0] imm_in,
  input  alu_in2_sel_in,
  input  [2:0] alu_op_in,
  input  [31:0] rs1_val_in,
  input  [31:0] rs2_val_in,
  input  [4:0] rs1_in,
  input  [4:0] rs2_in,
  input  is_cond_in,
  input  nextpc_is_branch_in,
  input  [2:0] funct3_in,
  input  mem_mode_in,
  input  [31:0] pcplus4_in,
  input  [1:0] rf_in_sel_in,
  input  [4:0] rd_in,
  input  flush,
  output [31:0] pc,
  output alu_in1_sel,
  output [31:0] imm,
  output alu_in2_sel,
  output [2:0] alu_op,
  output [31:0] rs1_val,
  output [31:0] rs2_val,
  output [4:0] rs1,
  output [4:0] rs2,
  output is_cond,
  output nextpc_is_branch,
  output [2:0] funct3,
  output mem_mode,
  output [31:0] pcplus4,
  output [1:0] rf_in_sel,
  output [4:0] rd
);
endmodule

module compare (
  input  [31:0] a,
  input  [31:0] b,
  input  [2:0] funct3,
  output result
);
endmodule

module exmem (
  input  [31:0] alu_out_in,
  input  [31:0] rs2_val_in,
  input  [2:0] funct3_in,
  input  mem_mode_in,
  input  [31:0] pcplus4_in,
  input  [1:0] rf_in_sel_in,
  input  [4:0] rd_in,
  output [31:0] alu_out,
  output [31:0] rs2_val,
  output [2:0] funct3,
  output mem_mode,
  output [31:0] pcplus4,
  output [1:0] rf_in_sel,
  output [4:0] rd
);
endmodule

module memwb (
  input  [31:0] alu_out_in,
  input  [31:0] mem_out_in,
  input  [31:0] pcplus4_in,
  input  [1:0] rf_in_sel_in,
  input  [4:0] rd_in,
  output [31:0] alu_out,
  output [31:0] mem_out,
  output [31:0] pcplus4,
  output [1:0] rf_in_sel,
  output [4:0] rd
);
endmodule

module forwarding (
  input  [1:0] rf_in_sel_wb,
  input  [4:0] rd_wb,
  input  [4:0] rd_mem,
  input  [1:0] rf_in_sel_mem,
  input  [4:0] rs1_ex,
  input  [4:0] rs2_ex,
  output [1:0] forward_rs2,
  output [1:0] forward_rs1
);
endmodule

module hazard (
  input  nextpc_is_branch_ex,
  input  [4:0] rd_ex,
  input  [1:0] rf_in_sel_ex,
  input  [4:0] rs2_id,
  input  [4:0] rs1_id,
  output id_ex_flush,
  output pc_we,
  output if_id_flush,
  output if_id_we
);
endmodule
